# Fritzing sketch nxtduino (saved by Fritzing 0.9.3b)
circuit board: 10.1776cm x 5.36194cm
breadboards: 1

parts:
  J2 = shrouded pin header, 6 pins [form="♂ (shrouded male)"]  # not connected
  U1 = LM 358 Dual Op-Amp [package="DIP8 [THT]"]
  U2 = Voltage Regulator - Variable [package="TO220 [THT]"]
  R1 = Resistor [tolerance=±5% resistance=240 package=THT]
  R2 = Resistor [tolerance=±2% resistance=680 package=THT]
  R3 = Resistor [tolerance=±5% resistance=200 package=THT]
  R4 = Resistor [tolerance=±5% resistance=1M package=THT]
  R5 = Resistor [tolerance=±5% resistance=10k package=THT]
  R6 = Resistor [tolerance=±5% resistance=1M package=THT]
  R7 = Resistor [tolerance=±5% resistance=10k package=THT]
  Bauteil1 = Arduino Mega 2560 (Rev3)
  J3 = shrouded pin header, 6 pins [form="♂ (shrouded male)"]  # not connected
  IC2 = L293D [package=THT]
  IC1 = L293D [package=THT]
  J4 = shrouded pin header, 6 pins [form="♂ (shrouded male)"]
  J5 = shrouded pin header, 6 pins [form="♂ (shrouded male)"]
  R8 = Resistor [tolerance=±5% resistance=1M package=THT]
  R9 = Resistor [tolerance=±5% resistance=1M package=THT]
  R10 = Resistor [tolerance=±5% resistance=10k package=THT]
  R11 = Resistor [tolerance=±5% resistance=10k package=THT]
  U3 = LM 358 Dual Op-Amp [package="DIP8 [THT]"]

nets (from the schematic view):
  N1: U1.connector0, R4.Pin_1, Bauteil1.A8
  N2: U1.connector1, R4.Pin_0, R5.Pin_1
  GND: U1.connector3, R3.Pin_1, R5.Pin_0, IC2.0V, IC1.0V, J5.pin3, J5.pin5, R11.Pin_0, U3.connector3
  N3: U1.connector5, R6.Pin_0, R7.Pin_1
  N4: U1.connector6, R6.Pin_1, Bauteil1.A9
  6,3V: U1.connector7, U2.OUT, R1.Pin_0, U3.connector7
  N5: U2.ADJ, R1.Pin_1, R2.Pin_0
  9V: U2.IN, Bauteil1.VIN, IC2.+Vmotor, IC1.+Vmotor
  N6: R2.Pin_1, R3.Pin_0
  N7: Bauteil1.A10, R9.Pin_1, U3.connector0
  N8: Bauteil1.A11, R8.Pin_1, U3.connector6
  SCL: Bauteil1.SCL, J5.pin6
  SDA: Bauteil1.SDA, J5.pin1, J5.pin4, U3.connector4
  N9: Bauteil1.D10_PWM, IC1.In_4
  N10: Bauteil1.D9_PWM, IC1.Enable_1
  N11: Bauteil1.D8_PWM, IC1.In_1
  5V: Bauteil1.5V, IC2.+V, IC1.+V, J5.pin2
  N12: Bauteil1.D4_PWM, IC2.In_1
  N13: Bauteil1.D5_PWM, IC2.Enable_1
  N14: Bauteil1.D6_PWM, IC2.In_4
  N15: Bauteil1.D7_PWM, IC1.In_2
  D22: Bauteil1.D22
  D23: Bauteil1.D23
  N16: Bauteil1.D24, IC2.In_2
  N17: Bauteil1.D27, IC2.Enable_2
  N18: Bauteil1.D28, IC2.In_3
  N19: Bauteil1.D29, IC1.Enable_2
  N20: Bauteil1.D30, IC1.In_3
  M_A1: IC2.Out_1_(_Controlled_by_Enable_1_)
  M_A2: IC2.Out_2_(_Controlled_by_Enable_1_)
  M_B2: IC2.Out_3_(_Controlled_by_Enable_2_)
  M_B1: IC2.Out_4_(_Controlled_by_Enable_2_)
  M_C1: IC1.Out_1_(_Controlled_by_Enable_1_)
  m_C2: IC1.Out_2_(_Controlled_by_Enable_1_)
  M_D2: IC1.Out_3_(_Controlled_by_Enable_2_)
  M_D1: IC1.Out_4_(_Controlled_by_Enable_2_)
  N21: J4.pin1, U3.connector2
  N22: R8.Pin_0, R11.Pin_1, U3.connector5
  N23: R9.Pin_0, R10.Pin_1, U3.connector1

notes:
  PORT D Ultrasonic
